// Digital circuit traffic_controller.dig as structural Verilog
module traffic_controller (
  input  clk,
  input  reset,
  input  in_3
);

  wire and_1_out, and_2_out, mg, mr, my, not_1_out, not_2_out, not_3_out, not_4_out, not_5_out, or_1_out, sg,
       sr, sy;

  LED led_1 (.in(mr));
  LED led_2 (.in(my));
  LED led_3 (.in(mg));
  LED led_4 (.in(sr));
  LED led_5 (.in(sy));
  LED led_6 (.in(sg));
  not not_1 (not_1_out, mg);
  not not_2 (not_2_out, sy);
  not not_3 (not_3_out, sg);
  not not_4 (not_4_out, mg);
  not not_5 (not_5_out, sy);
  and and_1 (and_1_out, not_4_out, not_5_out);
  or or_1 (or_1_out, mg, sy);
  and and_2 (and_2_out, not_1_out, not_2_out, not_3_out);
  D_FF_AS u_MR (.Set(reset), .D(and_1_out), .C(clk), .Clr(in_3), .Q(mr));  // open: nQ
  D_FF_AS u_MY (.Set(in_3), .D(mg), .C(clk), .Clr(reset), .Q(my));  // open: nQ
  D_FF_AS u_MG (.Set(in_3), .D(sy), .C(clk), .Clr(reset), .Q(mg));  // open: nQ
  D_FF_AS u_SR (.Set(reset), .D(or_1_out), .C(clk), .Clr(in_3), .Q(sr));  // open: nQ
  D_FF_AS u_SY (.Set(in_3), .D(sg), .C(clk), .Clr(reset), .Q(sy));  // open: nQ
  D_FF_AS u_SG (.Set(in_3), .D(and_2_out), .C(clk), .Clr(reset), .Q(sg));  // open: nQ

  // Other names for the same wires on the sheet: rst = reset
endmodule
